# Fritzing sketch button_switched_diode (saved by Fritzing 0.8.3b)
breadboards: 1

parts:
  Part1 = Arduino Uno (Rev3)
  S1 = Pushbutton [package="[THT]"]
  R1 = Resistor [tolerance=±5% resistance=10k package=THT]
  LED1 = LED - 5mm [color="Red (633nm)" package="5 mm [THT]"]
  R2 = Resistor [tolerance=±5% resistance=220 package=THT]

nets:
  N1: Part1.5V, S1.Pin_3, S1.Pin_4
  N2: Part1.D10_PWM/SS, R2.Pin_1
  N3: Part1.D7, S1.Pin_1, S1.Pin_2, R1.Pin_0
  N4: Part1.GND, R1.Pin_1, LED1.cathode
  N5: LED1.anode, R2.Pin_0
