# Fritzing sketch photocell_yun (saved by Fritzing 0.8.3b)
breadboards: 1

parts:
  Part1 = Arduino Due (Rev2b)
  R1 = Photocell (LDR) [package=THT]
  R2 = Resistor [tolerance=±5% resistance=10k package=THT]

nets:
  N1: Part1.A0, R1.pin_1
  N2: Part1.5V, R1.pin_0, R2.Pin_1
  N3: Part1.GND, R2.Pin_0
